# Fritzing sketch Trinket-M0+DFPlayer-UART (saved by Fritzing 0.9.3b)
stripboards: 2

parts:
  Bauteil1 = Adafruit Trinket M0 [part_number="Adafruit #3500"]
  DFPlayer_Mini1 = DFPlayer MINI [package="DIP (Dual Inline) [THT]"]
  S1 = Pushbutton [package="[THT]"]
  S2 = Pushbutton [package="[THT]"]
  J7 = male pin header, 3 pins [form="♂ (male)"]
  J6 = male pin header, 12 pins [form="♂ (male)"]
  J8 = male pin header, 5 pins [form="♂ (male)"]
  J4 = male pin header, 6 pins [form="♂ (male)"]
  J3 = male pin header, 10 pins [form="♂ (male)"]
  JS3 = Generic Jumper Shunt
  JS4 = Generic Jumper Shunt

nets:
  N1: Bauteil1.VBAT, Bauteil1.VBUS, DFPlayer_Mini1.VCC, DFPlayer_Mini1.BUSY, J6.pin2, J6.pin4, J6.pin5, J8.pin1, J4.pin1, J3.pin2, J3.pin3, JS3.pin1, JS3.pin2, JS4.pin1, JS4.pin2
  GND: Bauteil1.GND, Bauteil1.D0_A4_PA08_SDA, DFPlayer_Mini1.GND, S1.Pin_3, S1.Pin_4, S2.Pin_1, S2.Pin_2, J7.pin2, J6.pin1, J6.pin3, J6.pin11, J8.pin2, J4.pin2, J4.pin6, J3.pin1, J3.pin9
  N2: Bauteil1.D4_A2_PA06_TXD_MOSI, Bauteil1.D1_A0_PA02, DFPlayer_Mini1.RX, DFPlayer_Mini1.USB_-, J6.pin6, J8.pin3, J4.pin3, J3.pin4
  N3: Bauteil1.D3_A3_PA07_RXD_SCK, Bauteil1.D2_A1_PA09_SCL_MISO, DFPlayer_Mini1.TX, DFPlayer_Mini1.USB_+, J6.pin7, J8.pin4, J4.pin4, J3.pin5
  N4: Bauteil1.!RESET, Bauteil1.3.3V, J8.pin5, J4.pin5
  N5: DFPlayer_Mini1.DAC_R, DFPlayer_Mini1.K2/ADC_KEY, J6.pin8, J3.pin6
  N6: DFPlayer_Mini1.DAC_L, DFPlayer_Mini1.K1/ADC_KEY, J6.pin9, J3.pin7
  N7: DFPlayer_Mini1.SPK1, DFPlayer_Mini1.IO_2, S2.Pin_3, S2.Pin_4, J7.pin1, J6.pin10, J3.pin8
  N8: DFPlayer_Mini1.SPK2, DFPlayer_Mini1.IO_1, S1.Pin_1, S1.Pin_2, J7.pin3, J6.pin12, J3.pin10

custom parts:
  DFPlayer MINI: MP3 module by DFRobot.com for playing Music from an SD-Card. Supports WAV and MP3 files.
